# Fritzing sketch circuit (saved by Fritzing 0.9.3b)
breadboards: 1

parts:
  J1 = T Cobbler Plus
  IC1 = L293D [package=THT]
  M1 = Stepper Motor - Bipolar
  BAT1 = Battery Holders [package=battery-aa]
  LED1 = LED - 5mm [color="Green (565nm)" package="5 mm [THT]"]
  LED3 = LED - 5mm [color="Blue (430nm)" package="5 mm [THT]"]
  LED4 = LED - 5mm [color="Red (633nm)" package="5 mm [THT]"]
  LED5 = LED - 5mm [color="Green (565nm)" package="5 mm [THT]"]

nets:
  N1: J1.5.0V#1, IC1.+V
  N2: J1.GND#5, LED1.cathode, LED3.cathode, LED4.cathode, LED5.cathode
  N3: J1.#4, IC1.In_1
  N4: J1.#17, IC1.In_2
  N5: J1.#18, IC1.Enable_1, IC1.Enable_2
  N6: J1.#23, IC1.In_4
  N7: J1.#24, IC1.In_3
  N8: J1.GND#24, IC1.0V, BAT1.-
  N9: J1.#12, LED4.anode
  N10: J1.#19, LED3.anode
  N11: J1.#16, LED5.anode
  N12: J1.#26, LED1.anode
  N13: IC1.Out_1_(_Controlled_by_Enable_1_), M1.A
  N14: IC1.Out_2_(_Controlled_by_Enable_1_), M1.C
  N15: IC1.+Vmotor, BAT1.+
  N16: IC1.Out_3_(_Controlled_by_Enable_2_), M1.D
  N17: IC1.Out_4_(_Controlled_by_Enable_2_), M1.B

notes:
  12 VOLT BATTERY!
  <-- led_right
  <-- led_left
  <-- red_led
  <-- green_led

custom parts:
  T Cobbler Plus: The T-Cobbler Plus is an add on prototyping board from Adafruit specifically designed for the Raspberry Pi B+ that can break out all those tasty power, GPIO, I2C and SPI pins from the 40-pin header onto a solderless breadboard. This set will make "cobbling together" prototypes with the Pi super easy. The T-Cobbler Plus can plug into any solderless breadboard.
